// Logisim project cpu.circ as structural Verilog: 11 circuits, main circuit main
module main (
  input  in_1
);

  wire alu_3_is_zero, ALUinB, and_1_out, and_2_out, BReq, BRlt, clk, DMwe, inp, JP, JP_r, keyboard_1_avail,
       lt, memory_latch_1_oe_latched, memory_latch_1_we_latched, not_1_out, not_2_out, not_4_out, or_1_out,
       outp, Rdst, Rwd, Rwe;
  wire [2:0] ALUop, multiplexer_3_out, multiplexer_4_out;
  wire [6:0] keyboard_1_data;
  wire [7:0] keyout;
  wire [11:0] address;
  wire [14:0] alu_3_outp;
  wire [15:0] alu_1_outp, alu_2_outp, memory_latch_1_address_latched, memory_latch_1_data_in_latched,
       multiplexer_1_out, multiplexer_2_out, multiplexer_5_out, multiplexer_6_out, multiplexer_8_out,
       multiplexer_9_out, multiplexer_10_out, Program_count_outp, ram_1_dout, registerfile_1_data2, rsdata,
       sign_ext_1_extended;
  wire [15:12] rom_1_data;

  Multiplexer #(.width(16), .enable("false")) multiplexer_1 (
    .in0(multiplexer_8_out), .in1(rsdata), .out(multiplexer_1_out), .sel(JP_r));
  not not_1 (not_1_out, clk);
  Clock clock_1 (.out(clk));
  regi Program_count (.WE(1'b1), .clock(not_1_out), .reset(in_1), .inp(multiplexer_1_out), .outp(Program_count_outp));
  ROM #(.addrWidth(16), .dataWidth(16)) rom_1 (.addr(Program_count_outp), .data({rom_1_data, address}));
  alu alu_1 (.outp(alu_1_outp), .in2(16'h1), .in1(Program_count_outp), .ALUop(3'b000));  // open: shamt, is_zero
  control control_1 (
    .opcode(rom_1_data), .Rwd(Rwd), .RMwe(DMwe), .BReq(BReq), .BRlt(BRlt), .JP(JP), .JP_r(JP_r), .inp(inp),
    .outp(outp), .ALUinB(ALUinB), .Rwe(Rwe), .Rdst(Rdst), .ALUop(ALUop));
  Multiplexer #(.width(16), .enable("false")) multiplexer_2 (
    .in0(multiplexer_9_out), .in1(alu_1_outp), .out(multiplexer_2_out), .sel(JP));
  RegisterFile registerfile_1 (
    .write(multiplexer_3_out), .enable(Rwe), .read2(address[8:6]), .read1(address[11:9]), .reset(in_1),
    .clock(clk), .data(multiplexer_2_out), .data1(rsdata), .data2(registerfile_1_data2));
  Multiplexer #(.width(3), .enable("false")) multiplexer_3 (
    .in0(multiplexer_4_out), .in1(3'b111), .out(multiplexer_3_out), .sel(JP));
  Multiplexer #(.width(3), .enable("false")) multiplexer_4 (
    .in0(address[8:6]), .in1(address[5:3]), .out(multiplexer_4_out), .sel(Rdst));
  sign_ext sign_ext_1 (.extended(sign_ext_1_extended), .imme(address[5:0]));
  alu alu_2 (.outp(alu_2_outp), .in2(sign_ext_1_extended), .in1(alu_1_outp), .ALUop(3'b000));  // open: shamt, is_zero
  Multiplexer #(.width(16), .enable("false")) multiplexer_5 (
    .in0(registerfile_1_data2), .in1(sign_ext_1_extended), .out(multiplexer_5_out), .sel(ALUinB));
  TTY #(.rows(13), .cols(80)) tty_1 (.data(rsdata[6:0]), .clk(clk), .we(outp), .clr(in_1));
  and and_1 (and_1_out, BRlt, lt);
  alu alu_3 (
    .outp({lt, alu_3_outp}), .in2(multiplexer_5_out), .in1(rsdata), .shamt(address[2:0]), .ALUop(ALUop),
    .is_zero(alu_3_is_zero));
  Keyboard keyboard_1 (.clk(not_2_out), .re(inp), .clr(in_1), .avail(keyboard_1_avail), .data(keyboard_1_data));
  not not_2 (not_2_out, clk);
  and and_2 (and_2_out, BReq, alu_3_is_zero);
  or or_1 (or_1_out, and_2_out, and_1_out);
  Multiplexer #(.width(16), .enable("false")) multiplexer_6 (
    .in0(alu_1_outp), .in1(alu_2_outp), .out(multiplexer_6_out), .sel(or_1_out));
  not not_3 (keyout[7], keyboard_1_avail);
  not not_4 (not_4_out, clk);
  Multiplexer #(.width(7), .enable("false")) multiplexer_7 (
    .in0(keyboard_1_data), .in1({7{1'b0}}), .out(keyout[6:0]), .sel(keyout[7]));
  Multiplexer #(.width(16), .enable("false")) multiplexer_8 (
    .in0(multiplexer_6_out), .in1({multiplexer_6_out[15:12], address}), .out(multiplexer_8_out), .sel(JP));
  memory_latch memory_latch_1 (
    .address({lt, alu_3_outp}), .WE(DMwe), .clk(not_4_out), .data_in(registerfile_1_data2),
    .address_latched(memory_latch_1_address_latched), .WE_latched(memory_latch_1_we_latched),
    .OE_latched(memory_latch_1_oe_latched), .data_in_latched(memory_latch_1_data_in_latched));
  RAM #(.addrWidth(16), .dataWidth(16), .trigger("high"), .databus("bibus")) ram_1 (
    .addr(memory_latch_1_address_latched), .we(memory_latch_1_we_latched), .oe(memory_latch_1_oe_latched),
    .din(memory_latch_1_data_in_latched), .dout(ram_1_dout));
  Multiplexer #(.width(16), .enable("false")) multiplexer_9 (
    .in0(multiplexer_10_out), .in1({{8{1'b0}}, keyout}), .out(multiplexer_9_out), .sel(inp));
  Multiplexer #(.width(16), .enable("false")) multiplexer_10 (
    .in0({lt, alu_3_outp}), .in1(ram_1_dout), .out(multiplexer_10_out), .sel(Rwd));

  // Other names for the same wires on the sheet: Imme[5:0] = address[5:0]; shamt[2:0] = address[2:0];
  //   rd[2:0] = address[5:3]; rt[2:0] = address[8:6]; rs[2:0] = address[11:9]; reset = in_1

  // Notes on the sheet:
  //   contents of rom_1 (hex, n*v repeats v):
  //   204a e008 22a0 f400 e008 22a0 f400 e008 22a0 f400 903f 903f 219e 903f 219f 903f 207f 2144 a282 2198
  //   903f 2145
  //   R
  //   I
  //   J
endmodule

module regi (
  input  WE,
  input  clock,
  input  reset,
  input  [15:0] inp,
  output [15:0] outp
);

  wire clock_WE;

  and and_1 (clock_WE, WE, clock);
  D_Flip_Flop d_ff_1 (.D(inp[0]), .clk(clock_WE), .Q(outp[0]), .reset(reset));  // open: Qn, preset
  D_Flip_Flop d_ff_2 (.D(inp[1]), .clk(clock_WE), .Q(outp[1]), .reset(reset));  // open: Qn, preset
  D_Flip_Flop d_ff_3 (.D(inp[2]), .clk(clock_WE), .Q(outp[2]), .reset(reset));  // open: Qn, preset
  D_Flip_Flop d_ff_4 (.D(inp[3]), .clk(clock_WE), .Q(outp[3]), .reset(reset));  // open: Qn, preset
  D_Flip_Flop d_ff_5 (.D(inp[4]), .clk(clock_WE), .Q(outp[4]), .reset(reset));  // open: Qn, preset
  D_Flip_Flop d_ff_6 (.D(inp[5]), .clk(clock_WE), .Q(outp[5]), .reset(reset));  // open: Qn, preset
  D_Flip_Flop d_ff_7 (.D(inp[6]), .clk(clock_WE), .Q(outp[6]), .reset(reset));  // open: Qn, preset
  D_Flip_Flop d_ff_8 (.D(inp[7]), .clk(clock_WE), .Q(outp[7]), .reset(reset));  // open: Qn, preset
  D_Flip_Flop d_ff_9 (.D(inp[8]), .clk(clock_WE), .Q(outp[8]), .reset(reset));  // open: Qn, preset
  D_Flip_Flop d_ff_10 (.D(inp[9]), .clk(clock_WE), .Q(outp[9]), .reset(reset));  // open: Qn, preset
  D_Flip_Flop d_ff_11 (.D(inp[10]), .clk(clock_WE), .Q(outp[10]), .reset(reset));  // open: Qn, preset
  D_Flip_Flop d_ff_12 (.D(inp[11]), .clk(clock_WE), .Q(outp[11]), .reset(reset));  // open: Qn, preset
  D_Flip_Flop d_ff_13 (.D(inp[12]), .clk(clock_WE), .Q(outp[12]), .reset(reset));  // open: Qn, preset
  D_Flip_Flop d_ff_14 (.D(inp[13]), .clk(clock_WE), .Q(outp[13]), .reset(reset));  // open: Qn, preset
  D_Flip_Flop d_ff_15 (.D(inp[14]), .clk(clock_WE), .Q(outp[14]), .reset(reset));  // open: Qn, preset
  D_Flip_Flop d_ff_16 (.D(inp[15]), .clk(clock_WE), .Q(outp[15]), .reset(reset));  // open: Qn, preset

  // Other names for the same wires on the sheet: zero = inp[0]; one = inp[1]; two = inp[2]; three = inp[3];
  //   four = inp[4]; five = inp[5]; six = inp[6]; sev = inp[7]; eight = inp[8]; nine = inp[9]; ten = inp[10];
  //   elev = inp[11]; twelv = inp[12]; thirt = inp[13]; fourt = inp[14]; fift = inp[15]; out0 = outp[0];
  //   out1 = outp[1]; out2 = outp[2]; out3 = outp[3]; out4 = outp[4]; out5 = outp[5]; out6 = outp[6]; out7 = outp[7];
  //   out8 = outp[8]; out9 = outp[9]; outX = outp[10]; outX1 = outp[11]; outX2 = outp[12]; outX3 = outp[13];
  //   outX4 = outp[14]; outX5 = outp[15]
endmodule

module RegisterFile (
  input  [15:0] data,
  input  clock,
  input  reset,
  input  [2:0] read1,
  input  [2:0] read2,
  input  enable,
  input  [2:0] write,
  output [15:0] data1,
  output [15:0] data2
);

  wire read0_1, read0_2, read1_1, read1_2, read2_1, read2_2, read3_1, read3_2, read4_1, read4_2, read5_1,
       read5_2, read6_1, read6_2, read7_1, read7_2, write0, write1, write2, write3, write4, write5, write6,
       write7;
  wire [15:0] reg0_outp, reg1_outp, reg2_outp, reg3_outp, reg4_outp, reg5_outp, reg6_outp, reg7_outp;

  Decoder #(.select(3), .enable("false")) decoder_1 (
    .out0(read0_1), .out1(read1_1), .out2(read2_1), .out3(read3_1), .out4(read4_1), .out5(read5_1),
    .out6(read6_1), .out7(read7_1), .sel(read1));
  Decoder #(.select(3), .enable("false")) decoder_2 (
    .out0(read0_2), .out1(read1_2), .out2(read2_2), .out3(read3_2), .out4(read4_2), .out5(read5_2),
    .out6(read6_2), .out7(read7_2), .sel(read2));
  Decoder #(.select(3)) decoder_3 (
    .out0(write0), .out1(write1), .out2(write2), .out3(write3), .out4(write4), .out5(write5), .out6(write6),
    .out7(write7), .sel(write), .en(enable));
  assign data1 = read0_1 ? reg0_outp : 16'bz;  // Controlled_Buffer controlled_buffer_1
  regi reg0 (.clock(clock), .reset(reset), .inp(data), .outp(reg0_outp));  // open: WE
  assign data2 = read0_2 ? reg0_outp : 16'bz;  // Controlled_Buffer controlled_buffer_2
  // Probe on reg0_outp
  assign data1 = read1_1 ? reg1_outp : 16'bz;  // Controlled_Buffer controlled_buffer_3
  assign data2 = read1_2 ? reg1_outp : 16'bz;  // Controlled_Buffer controlled_buffer_4
  regi reg1 (.WE(write1), .clock(clock), .reset(reset), .inp(data), .outp(reg1_outp));
  // Probe on reg1_outp
  assign data1 = read2_1 ? reg2_outp : 16'bz;  // Controlled_Buffer controlled_buffer_5
  regi reg2 (.WE(write2), .clock(clock), .reset(reset), .inp(data), .outp(reg2_outp));
  assign data2 = read2_2 ? reg2_outp : 16'bz;  // Controlled_Buffer controlled_buffer_6
  // Probe on reg2_outp
  assign data1 = read3_1 ? reg3_outp : 16'bz;  // Controlled_Buffer controlled_buffer_7
  regi reg3 (.WE(write3), .clock(clock), .reset(reset), .inp(data), .outp(reg3_outp));
  assign data2 = read3_2 ? reg3_outp : 16'bz;  // Controlled_Buffer controlled_buffer_8
  // Probe on reg3_outp
  assign data1 = read4_1 ? reg4_outp : 16'bz;  // Controlled_Buffer controlled_buffer_9
  regi reg4 (.WE(write4), .clock(clock), .reset(reset), .inp(data), .outp(reg4_outp));
  assign data2 = read4_2 ? reg4_outp : 16'bz;  // Controlled_Buffer controlled_buffer_10
  // Probe on reg4_outp
  assign data1 = read5_1 ? reg5_outp : 16'bz;  // Controlled_Buffer controlled_buffer_11
  regi reg5 (.WE(write5), .clock(clock), .reset(reset), .inp(data), .outp(reg5_outp));
  assign data2 = read5_2 ? reg5_outp : 16'bz;  // Controlled_Buffer controlled_buffer_12
  // Probe on reg5_outp
  assign data1 = read6_1 ? reg6_outp : 16'bz;  // Controlled_Buffer controlled_buffer_13
  regi reg6 (.WE(write6), .clock(clock), .reset(reset), .inp(data), .outp(reg6_outp));
  assign data2 = read6_2 ? reg6_outp : 16'bz;  // Controlled_Buffer controlled_buffer_14
  // Probe on reg6_outp
  assign data1 = read7_1 ? reg7_outp : 16'bz;  // Controlled_Buffer controlled_buffer_15
  regi reg7 (.WE(write7), .clock(clock), .reset(reset), .inp(data), .outp(reg7_outp));
  assign data2 = read7_2 ? reg7_outp : 16'bz;  // Controlled_Buffer controlled_buffer_16
  // Probe on reg7_outp
endmodule

module memory_latch (
  input  [15:0] address,
  input  WE,
  input  clk,
  input  [15:0] data_in,
  output [15:0] address_latched,
  output WE_latched,
  output OE_latched,
  output [15:0] data_in_latched
);

  wire DMwe_latch_q;
  wire [15:0] addr_latch_q;

  Register #(.width(16), .trigger("falling")) addr_latch (
    .D(address), .en(WE), .clk(clk), .Q(addr_latch_q));  // open: clr
  D_Flip_Flop #(.trigger("falling")) DMwe_latch (.D(WE), .clk(clk), .Q(DMwe_latch_q));  // open: Qn, preset, reset
  Register #(.width(16), .trigger("falling")) data_to_be_written (
    .D(data_in), .en(WE), .clk(clk), .Q(data_in_latched));  // open: clr
  Multiplexer #(.width(16), .enable("false")) multiplexer_1 (
    .in0(address), .in1(addr_latch_q), .out(address_latched), .sel(DMwe_latch_q));
  and and_1 (WE_latched, clk, DMwe_latch_q);
  not not_1 (OE_latched, WE_latched);
endmodule

module fulladder (
  input  sub,
  input  [15:0] A,
  input  [15:0] B,
  output [15:0] result,
  output is_zero,
  output ovf
);

  wire and_1_out, and_2_out, and_3_out, and_4_out, and_5_out, and_6_out, and_7_out, and_8_out, and_9_out,
       and_10_out, and_11_out, and_12_out, and_13_out, and_14_out, and_15_out, and_16_out, and_17_out,
       and_18_out, and_19_out, and_20_out, and_21_out, and_22_out, and_23_out, and_24_out, and_25_out,
       and_26_out, and_27_out, and_28_out, and_29_out, and_30_out, and_31_out, and_32_out, or_1_out,
       or_2_out, or_3_out, or_4_out, or_5_out, or_6_out, or_7_out, or_8_out, or_9_out, or_10_out, or_11_out,
       or_12_out, or_13_out, or_14_out, or_15_out, or_16_out, or_17_out, Six_out, xor_3_out, xor_4_out,
       xor_6_out, xor_7_out, xor_9_out, xor_10_out, xor_12_out, xor_13_out, xor_15_out, xor_16_out,
       xor_18_out, xor_19_out, xor_21_out, xor_22_out, xor_24_out, xor_25_out, xor_27_out, xor_28_out,
       xor_30_out, xor_31_out, xor_33_out, xor_35_out, xor_36_out, xor_38_out, xor_39_out, xor_40_out,
       xor_42_out, xor_43_out, xor_45_out, xor_47_out, xor_48_out;

  or or_1 (or_1_out, and_1_out, and_2_out);
  xor xor_1 (ovf, or_1_out, or_2_out);
  and and_1 (and_1_out, xor_3_out, or_2_out);
  and and_2 (and_2_out, xor_4_out, A[15]);
  xor xor_2 (result[15], xor_3_out, or_2_out);
  or or_2 (or_2_out, and_3_out, and_4_out);
  xor xor_3 (xor_3_out, xor_4_out, A[15]);
  and and_3 (and_3_out, xor_6_out, or_3_out);
  and and_4 (and_4_out, xor_7_out, A[14]);
  xor xor_4 (xor_4_out, sub, B[15]);
  xor xor_5 (result[14], xor_6_out, or_3_out);
  or or_3 (or_3_out, and_5_out, and_6_out);
  xor xor_6 (xor_6_out, xor_7_out, A[14]);
  and and_5 (and_5_out, xor_9_out, or_4_out);
  and and_6 (and_6_out, xor_10_out, A[13]);
  xor xor_7 (xor_7_out, sub, B[14]);
  xor xor_8 (result[13], xor_9_out, or_4_out);
  or or_4 (or_4_out, and_7_out, and_8_out);
  xor xor_9 (xor_9_out, xor_10_out, A[13]);
  and and_7 (and_7_out, xor_12_out, or_5_out);
  and and_8 (and_8_out, xor_13_out, A[12]);
  xor xor_10 (xor_10_out, sub, B[13]);
  xor xor_11 (result[12], xor_12_out, or_5_out);
  xor xor_12 (xor_12_out, xor_13_out, A[12]);
  and and_9 (and_9_out, xor_15_out, or_6_out);
  or or_5 (or_5_out, and_9_out, and_10_out);
  and and_10 (and_10_out, xor_16_out, A[11]);
  xor xor_13 (xor_13_out, sub, B[12]);
  xor xor_14 (result[11], xor_15_out, or_6_out);
  xor xor_15 (xor_15_out, xor_16_out, A[11]);
  or or_6 (or_6_out, and_11_out, and_12_out);
  and and_11 (and_11_out, xor_18_out, or_7_out);
  and and_12 (and_12_out, xor_19_out, A[10]);
  xor xor_16 (xor_16_out, sub, B[11]);
  xor xor_17 (result[10], xor_18_out, or_7_out);
  or or_7 (or_7_out, and_13_out, and_14_out);
  xor xor_18 (xor_18_out, xor_19_out, A[10]);
  and and_13 (and_13_out, xor_21_out, or_8_out);
  and and_14 (and_14_out, xor_22_out, A[9]);
  xor xor_19 (xor_19_out, sub, B[10]);
  xor xor_20 (result[9], xor_21_out, or_8_out);
  or or_8 (or_8_out, and_15_out, and_16_out);
  xor xor_21 (xor_21_out, xor_22_out, A[9]);
  and and_15 (and_15_out, xor_24_out, or_9_out);
  and and_16 (and_16_out, xor_25_out, A[8]);
  xor xor_22 (xor_22_out, sub, B[9]);
  xor xor_23 (result[8], xor_24_out, or_9_out);
  xor xor_24 (xor_24_out, xor_25_out, A[8]);
  and and_17 (and_17_out, xor_27_out, or_10_out);
  or or_9 (or_9_out, and_17_out, and_18_out);
  and and_18 (and_18_out, xor_28_out, A[7]);
  xor xor_25 (xor_25_out, sub, B[8]);
  xor xor_26 (result[7], xor_27_out, or_10_out);
  xor xor_27 (xor_27_out, xor_28_out, A[7]);
  or or_10 (or_10_out, and_19_out, and_20_out);
  and and_19 (and_19_out, xor_30_out, or_11_out);
  and and_20 (and_20_out, xor_31_out, A[6]);
  xor xor_28 (xor_28_out, sub, B[7]);
  xor xor_29 (result[6], xor_30_out, or_11_out);
  or or_11 (or_11_out, and_21_out, and_22_out);
  xor xor_30 (xor_30_out, xor_31_out, A[6]);
  and and_21 (and_21_out, Six_out, or_12_out);
  and and_22 (and_22_out, xor_33_out, A[5]);
  xor xor_31 (xor_31_out, sub, B[6]);
  xor xor_32 (result[5], Six_out, or_12_out);
  or or_12 (or_12_out, and_23_out, and_24_out);
  xor Six (Six_out, xor_33_out, A[5]);
  and and_23 (and_23_out, xor_35_out, or_14_out);
  and and_24 (and_24_out, xor_36_out, A[4]);
  xor xor_33 (xor_33_out, sub, B[5]);
  or or_13 (or_13_out, result[0], result[1], result[2], result[3], result[4], result[5], result[6], result[7], result[8], result[9], result[10], result[11], result[12], result[13], result[14], result[15]);
  xor xor_34 (result[4], xor_35_out, or_14_out);
  or or_14 (or_14_out, and_25_out, and_26_out);
  xor xor_35 (xor_35_out, xor_36_out, A[4]);
  not not_1 (is_zero, or_13_out);
  and and_25 (and_25_out, xor_38_out, or_15_out);
  and and_26 (and_26_out, xor_39_out, A[3]);
  xor xor_36 (xor_36_out, sub, B[4]);
  xor xor_37 (result[3], xor_38_out, or_15_out);
  xor xor_38 (xor_38_out, xor_39_out, A[3]);
  xor xor_39 (xor_39_out, sub, B[3]);
  and and_27 (and_27_out, xor_40_out, or_16_out);
  or or_15 (or_15_out, and_27_out, and_28_out);
  and and_28 (and_28_out, xor_42_out, A[2]);
  xor xor_40 (xor_40_out, xor_42_out, A[2]);
  xor xor_41 (result[2], xor_40_out, or_16_out);
  or or_16 (or_16_out, and_29_out, and_30_out);
  xor xor_42 (xor_42_out, sub, B[2]);
  and and_29 (and_29_out, xor_45_out, or_17_out);
  and and_30 (and_30_out, xor_43_out, A[1]);
  xor xor_43 (xor_43_out, sub, B[1]);
  xor xor_44 (result[1], xor_45_out, or_17_out);
  or or_17 (or_17_out, and_31_out, and_32_out);
  xor xor_45 (xor_45_out, xor_43_out, A[1]);
  and and_31 (and_31_out, xor_48_out, sub);
  and and_32 (and_32_out, xor_47_out, A[0]);
  xor xor_46 (result[0], xor_48_out, sub);
  xor xor_47 (xor_47_out, sub, B[0]);
  xor xor_48 (xor_48_out, xor_47_out, A[0]);
endmodule

module Instruc_decoder (
  input  [3:0] op
);

  wire add, addi, beqz, blt, inp, j, jal, jr, lw, no, outp, shl, shr, sub, sw, x_or;

  Decoder #(.select(4), .enable("false")) decoder_1 (
    .out0(add), .out1(sub), .out2(addi), .out3(no), .out4(x_or), .out5(shl), .out6(shr), .out7(lw),
    .out8(sw), .out9(beqz), .out10(blt), .out11(j), .out12(jr), .out13(jal), .out14(inp), .out15(outp),
    .sel(op));
endmodule

module sign_ext (
  input  [5:0] imme,
  output [15:0] extended
);

  Multiplexer #(.width(10), .enable("false")) multiplexer_1 (
    .in0({10{1'b0}}), .in1({10{1'b1}}), .out(extended[15:6]), .sel(imme[5]));

  assign extended[5:0] = imme;

  // Other names for the same wires on the sheet: neg_ex = imme[5]
endmodule

module shiftright (
  input  [15:0] inp,
  input  [2:0] shamt,
  output [15:0] outp
);

  Multiplexer #(.select(3), .enable("false")) multiplexer_1 (
    .in0(inp[0]), .in1(inp[1]), .in2(inp[2]), .in3(inp[3]), .in4(inp[4]), .in5(inp[5]), .in6(inp[6]),
    .in7(inp[7]), .out(outp[0]), .sel(shamt));
  Multiplexer #(.select(3), .enable("false")) multiplexer_2 (
    .in0(inp[1]), .in1(inp[2]), .in2(inp[3]), .in3(inp[4]), .in4(inp[5]), .in5(inp[6]), .in6(inp[7]),
    .in7(inp[8]), .out(outp[1]), .sel(shamt));
  Multiplexer #(.select(3), .enable("false")) multiplexer_3 (
    .in0(inp[2]), .in1(inp[3]), .in2(inp[4]), .in3(inp[5]), .in4(inp[6]), .in5(inp[7]), .in6(inp[8]),
    .in7(inp[9]), .out(outp[2]), .sel(shamt));
  Multiplexer #(.select(3), .enable("false")) multiplexer_4 (
    .in0(inp[3]), .in1(inp[4]), .in2(inp[5]), .in3(inp[6]), .in4(inp[7]), .in5(inp[8]), .in6(inp[9]),
    .in7(inp[10]), .out(outp[3]), .sel(shamt));
  Multiplexer #(.select(3), .enable("false")) multiplexer_5 (
    .in0(inp[4]), .in1(inp[5]), .in2(inp[6]), .in3(inp[7]), .in4(inp[8]), .in5(inp[9]), .in6(inp[10]),
    .in7(inp[11]), .out(outp[4]), .sel(shamt));
  Multiplexer #(.select(3), .enable("false")) multiplexer_6 (
    .in0(inp[5]), .in1(inp[6]), .in2(inp[7]), .in3(inp[8]), .in4(inp[9]), .in5(inp[10]), .in6(inp[11]),
    .in7(inp[12]), .out(outp[5]), .sel(shamt));
  Multiplexer #(.select(3), .enable("false")) multiplexer_7 (
    .in0(inp[6]), .in1(inp[7]), .in2(inp[8]), .in3(inp[9]), .in4(inp[10]), .in5(inp[11]), .in6(inp[12]),
    .in7(inp[13]), .out(outp[6]), .sel(shamt));
  Multiplexer #(.select(3), .enable("false")) multiplexer_8 (
    .in0(inp[7]), .in1(inp[8]), .in2(inp[9]), .in3(inp[10]), .in4(inp[11]), .in5(inp[12]), .in6(inp[13]),
    .in7(inp[14]), .out(outp[7]), .sel(shamt));
  Multiplexer #(.select(3), .enable("false")) multiplexer_9 (
    .in0(inp[8]), .in1(inp[9]), .in2(inp[10]), .in3(inp[11]), .in4(inp[12]), .in5(inp[13]), .in6(inp[14]),
    .in7(inp[15]), .out(outp[8]), .sel(shamt));
  Multiplexer #(.select(3), .enable("false")) multiplexer_10 (
    .in0(inp[9]), .in1(inp[10]), .in2(inp[11]), .in3(inp[12]), .in4(inp[13]), .in5(inp[14]), .in6(inp[15]),
    .in7(1'b0), .out(outp[9]), .sel(shamt));
  Multiplexer #(.select(3), .enable("false")) multiplexer_11 (
    .in0(inp[10]), .in1(inp[11]), .in2(inp[12]), .in3(inp[13]), .in4(inp[14]), .in5(inp[15]), .in6(1'b0),
    .in7(1'b0), .out(outp[10]), .sel(shamt));
  Multiplexer #(.select(3), .enable("false")) multiplexer_12 (
    .in0(inp[11]), .in1(inp[12]), .in2(inp[13]), .in3(inp[14]), .in4(inp[15]), .in5(1'b0), .in6(1'b0),
    .in7(1'b0), .out(outp[11]), .sel(shamt));
  Multiplexer #(.select(3), .enable("false")) multiplexer_13 (
    .in0(inp[12]), .in1(inp[13]), .in2(inp[14]), .in3(inp[15]), .in4(1'b0), .in5(1'b0), .in6(1'b0),
    .in7(1'b0), .out(outp[12]), .sel(shamt));
  Multiplexer #(.select(3), .enable("false")) multiplexer_14 (
    .in0(inp[13]), .in1(inp[14]), .in2(inp[15]), .in3(1'b0), .in4(1'b0), .in5(1'b0), .in6(1'b0), .in7(1'b0),
    .out(outp[13]), .sel(shamt));
  Multiplexer #(.select(3), .enable("false")) multiplexer_15 (
    .in0(inp[14]), .in1(inp[15]), .in2(1'b0), .in3(1'b0), .in4(1'b0), .in5(1'b0), .in6(1'b0), .in7(1'b0),
    .out(outp[14]), .sel(shamt));
  Multiplexer #(.select(3), .enable("false")) multiplexer_16 (
    .in0(inp[15]), .in1(1'b0), .in2(1'b0), .in3(1'b0), .in4(1'b0), .in5(1'b0), .in6(1'b0), .in7(1'b0),
    .out(outp[15]), .sel(shamt));

  // Other names for the same wires on the sheet: zero = inp[0]; one = inp[1]; two = inp[2]; three = inp[3];
  //   four = inp[4]; five = inp[5]; six = inp[6]; seven = inp[7]; eight = inp[8]; nine = inp[9]; ten = inp[10];
  //   ele = inp[11]; tw = inp[12]; thir = inp[13]; fourt = inp[14]; fif = inp[15]; ling = outp[0]; yi = outp[1];
  //   er = outp[2]; san = outp[3]; si = outp[4]; wu = outp[5]; liu = outp[6]; qi = outp[7]; ba = outp[8];
  //   jiu = outp[9]; shi = outp[10]; syi = outp[11]; ser = outp[12]; ssan = outp[13]; ssi = outp[14]; swu = outp[15]
endmodule

module shiftleft (
  input  [15:0] in_1,
  input  [2:0] in_2,
  output [15:0] out_3
);

  Multiplexer #(.select(3), .enable("false")) multiplexer_1 (
    .in0(in_1[0]), .in1(1'b0), .in2(1'b0), .in3(1'b0), .in4(1'b0), .in5(1'b0), .in6(1'b0), .in7(1'b0),
    .out(out_3[0]), .sel(in_2));
  Multiplexer #(.select(3), .enable("false")) multiplexer_2 (
    .in0(in_1[1]), .in1(in_1[0]), .in2(1'b0), .in3(1'b0), .in4(1'b0), .in5(1'b0), .in6(1'b0), .in7(1'b0),
    .out(out_3[1]), .sel(in_2));
  Multiplexer #(.select(3), .enable("false")) multiplexer_3 (
    .in0(in_1[2]), .in1(in_1[1]), .in2(in_1[0]), .in3(1'b0), .in4(1'b0), .in5(1'b0), .in6(1'b0), .in7(1'b0),
    .out(out_3[2]), .sel(in_2));
  Multiplexer #(.select(3), .enable("false")) multiplexer_4 (
    .in0(in_1[3]), .in1(in_1[2]), .in2(in_1[1]), .in3(in_1[0]), .in4(1'b0), .in5(1'b0), .in6(1'b0),
    .in7(1'b0), .out(out_3[3]), .sel(in_2));
  Multiplexer #(.select(3), .enable("false")) multiplexer_5 (
    .in0(in_1[4]), .in1(in_1[3]), .in2(in_1[2]), .in3(in_1[1]), .in4(in_1[0]), .in5(1'b0), .in6(1'b0),
    .in7(1'b0), .out(out_3[4]), .sel(in_2));
  Multiplexer #(.select(3), .enable("false")) multiplexer_6 (
    .in0(in_1[5]), .in1(in_1[4]), .in2(in_1[3]), .in3(in_1[2]), .in4(in_1[1]), .in5(in_1[0]), .in6(1'b0),
    .in7(1'b0), .out(out_3[5]), .sel(in_2));
  Multiplexer #(.select(3), .enable("false")) multiplexer_7 (
    .in0(in_1[6]), .in1(in_1[5]), .in2(in_1[4]), .in3(in_1[3]), .in4(in_1[2]), .in5(in_1[1]), .in6(in_1[0]),
    .in7(1'b0), .out(out_3[6]), .sel(in_2));
  Multiplexer #(.select(3), .enable("false")) multiplexer_8 (
    .in0(in_1[7]), .in1(in_1[6]), .in2(in_1[5]), .in3(in_1[4]), .in4(in_1[3]), .in5(in_1[2]), .in6(in_1[1]),
    .in7(in_1[0]), .out(out_3[7]), .sel(in_2));
  Multiplexer #(.select(3), .enable("false")) multiplexer_9 (
    .in0(in_1[8]), .in1(in_1[7]), .in2(in_1[6]), .in3(in_1[5]), .in4(in_1[4]), .in5(in_1[3]), .in6(in_1[2]),
    .in7(in_1[1]), .out(out_3[8]), .sel(in_2));
  Multiplexer #(.select(3), .enable("false")) multiplexer_10 (
    .in0(in_1[9]), .in1(in_1[8]), .in2(in_1[7]), .in3(in_1[6]), .in4(in_1[5]), .in5(in_1[4]), .in6(in_1[3]),
    .in7(in_1[2]), .out(out_3[9]), .sel(in_2));
  Multiplexer #(.select(3), .enable("false")) multiplexer_11 (
    .in0(in_1[10]), .in1(in_1[9]), .in2(in_1[8]), .in3(in_1[7]), .in4(in_1[6]), .in5(in_1[5]), .in6(in_1[4]),
    .in7(in_1[3]), .out(out_3[10]), .sel(in_2));
  Multiplexer #(.select(3), .enable("false")) multiplexer_12 (
    .in0(in_1[11]), .in1(in_1[10]), .in2(in_1[9]), .in3(in_1[8]), .in4(in_1[7]), .in5(in_1[6]),
    .in6(in_1[5]), .in7(in_1[4]), .out(out_3[11]), .sel(in_2));
  Multiplexer #(.select(3), .enable("false")) multiplexer_13 (
    .in0(in_1[12]), .in1(in_1[11]), .in2(in_1[10]), .in3(in_1[9]), .in4(in_1[8]), .in5(in_1[7]),
    .in6(in_1[6]), .in7(in_1[5]), .out(out_3[12]), .sel(in_2));
  Multiplexer #(.select(3), .enable("false")) multiplexer_14 (
    .in0(in_1[13]), .in1(in_1[12]), .in2(in_1[11]), .in3(in_1[10]), .in4(in_1[9]), .in5(in_1[8]),
    .in6(in_1[7]), .in7(in_1[6]), .out(out_3[13]), .sel(in_2));
  Multiplexer #(.select(3), .enable("false")) multiplexer_15 (
    .in0(in_1[14]), .in1(in_1[13]), .in2(in_1[12]), .in3(in_1[11]), .in4(in_1[10]), .in5(in_1[9]),
    .in6(in_1[8]), .in7(in_1[7]), .out(out_3[14]), .sel(in_2));
  Multiplexer #(.select(3), .enable("false")) multiplexer_16 (
    .in0(in_1[15]), .in1(in_1[14]), .in2(in_1[13]), .in3(in_1[12]), .in4(in_1[11]), .in5(in_1[10]),
    .in6(in_1[9]), .in7(in_1[8]), .out(out_3[15]), .sel(in_2));

  // Other names for the same wires on the sheet: inp[15:0] = in_1; zero = in_1[0]; one = in_1[1]; two = in_1[2];
  //   three = in_1[3]; four = in_1[4]; five = in_1[5]; six = in_1[6]; seven = in_1[7]; eight = in_1[8];
  //   nine = in_1[9]; ten = in_1[10]; ele = in_1[11]; tw = in_1[12]; thir = in_1[13]; fourt = in_1[14];
  //   fif = in_1[15]; ling = out_3[0]; outp[15:0] = out_3; yi = out_3[1]; er = out_3[2]; san = out_3[3];
  //   si = out_3[4]; wu = out_3[5]; liu = out_3[6]; qi = out_3[7]; ba = out_3[8]; jiu = out_3[9]; shi = out_3[10];
  //   syi = out_3[11]; ser = out_3[12]; ssan = out_3[13]; ssi = out_3[14]; swu = out_3[15]; shamt[2:0] = in_2
endmodule

module alu (
  input  [2:0] ALUop,
  input  [2:0] shamt,
  input  [15:0] in1,
  input  [15:0] in2,
  output [15:0] outp,
  output is_zero
);

  wire sub;
  wire [15:0] outadder, outnot, outsll, outsrl, outxor;

  Multiplexer #(.select(3), .width(16), .enable("false")) multiplexer_1 (
    .in0(outadder), .in1(outadder), .in2(outsrl), .in3(outsll), .in4(outnot), .in5(outxor), .out(outp),
    .sel(ALUop));  // open: in6, in7
  // Probe on outp
  Decoder #(.select(3), .enable("false")) decoder_1 (
    .out1(sub), .sel(ALUop));  // open: out0, out2, out3, out4, out5, out6, out7
  assign outnot = ~in1;  // NOT_Gate not_1, 16 bits wide
  assign outxor = in1 ^ in2;  // XOR_Gate xor_1, 16 bits wide
  fulladder fulladder_1 (.sub(sub), .A(in1), .B(in2), .result(outadder), .is_zero(is_zero));  // open: ovf
  shiftleft shiftleft_1 (.in_1(in1), .in_2(shamt), .out_3(outsll));
  shiftright shiftright_1 (.inp(in1), .shamt(shamt), .outp(outsrl));

  // Other names for the same wires on the sheet: op[2:0] = ALUop

  // Notes on the sheet:
  //   Add_Addi_Sub
  //   Not
  //   Xor
  //   Sll
  //   Srl
endmodule

module control (
  input  [3:0] opcode,
  output Rwd,
  output RMwe,
  output BReq,
  output BRlt,
  output JP,
  output JP_r,
  output inp,
  output outp,
  output ALUinB,
  output Rwe,
  output Rdst,
  output [2:0] ALUop
);

  wire add, addi, exor, j, jal, no, sII, srI, sub;

  Decoder #(.select(4), .enable("false")) decoder_1 (
    .out0(add), .out1(sub), .out2(addi), .out3(no), .out4(exor), .out5(sII), .out6(srI), .out7(Rwd),
    .out8(RMwe), .out9(BReq), .out10(BRlt), .out11(j), .out12(JP_r), .out13(jal), .out14(inp), .out15(outp),
    .sel(opcode));
  or or_1 (Rwe, add, sub, no, exor, sII, srI, inp, addi, Rwd, inp, jal);
  or or_2 (JP, j, JP_r, jal);
  or or_3 (ALUop[1], srI, sII);
  or or_4 (ALUop[2], no, exor);
  or or_5 (ALUop[0], BReq, exor, sub, sII, BRlt);
  or or_6 (ALUinB, Rwd, addi, RMwe);
  or or_7 (Rdst, add, sub, no, exor, sII, srI, inp);

  // Other names for the same wires on the sheet: beqz = BReq; blt = BRlt; jr = JP_r; lw = Rwd; sw = RMwe
endmodule
