// Logisim project robot.circ as structural Verilog: 1 circuit, main circuit main
module main (
  input  in_stopall,
  input  in_stopupdown,
  output out_tired,
  output out_1D,
  output out_2D
);

  wire and_1_out, and_2_out, and_3_out, and_4_out, clock_1_out, not_1_out, not_2_out, not_3_out, not_4_out,
       not_5_out, not_6_out, not_7_out, not_8_out;

  not not_1 (not_1_out, in_stopall);
  not not_2 (not_2_out, in_stopall);
  and and_1 (and_1_out, not_2_out, in_stopupdown);
  not not_3 (not_3_out, in_stopall);
  and and_2 (and_2_out, not_3_out, not_4_out);
  not not_4 (not_4_out, in_stopupdown);
  and and_3 (and_3_out, not_1_out, not_5_out);
  D_Flip_Flop QD0 (.D(and_3_out), .clk(clock_1_out), .Q(out_tired));  // open: Qn, preset, reset
  D_Flip_Flop QD1 (.D(and_1_out), .clk(clock_1_out), .Q(out_1D));  // open: Qn, preset, reset
  D_Flip_Flop QD2 (.D(and_2_out), .clk(clock_1_out), .Q(out_2D));  // open: Qn, preset, reset
  Clock clock_1 (.out(clock_1_out));
  not not_5 (not_5_out, and_4_out);
  and and_4 (and_4_out, not_6_out, not_7_out, not_8_out);
  not not_6 (not_6_out, out_2D);
  not not_7 (not_7_out, out_1D);
  not not_8 (not_8_out, out_tired);
endmodule
